// Logisim project control-logic.circ as structural Verilog: 1 circuit, main circuit control_logic
module control_logic (
  input  [31:0] Instruction,
  input  BrEq,
  input  BrLt,
  output PCSel,
  output RegWEn,
  output [2:0] ImmSel,
  output BrUn,
  output ASel,
  output BSel,
  output [3:0] ALUSel,
  output MemWEn,
  output [1:0] WBSel
);

  wire and_22_out, and_23_out, and_24_out, and_25_out, and_26_out, and_27_out, BType, comparator_10_eq,
       comparator_11_eq, comparator_12_eq, comparator_13_eq, comparator_14_eq, comparator_15_eq,
       comparator_16_eq, comparator_17_eq, comparator_18_eq, comparator_19_eq, comparator_20_eq,
       comparator_21_eq, comparator_22_eq, comparator_23_eq, comparator_24_eq, comparator_25_eq,
       comparator_26_eq, comparator_27_eq, comparator_28_eq, comparator_29_eq, comparator_30_eq,
       comparator_31_eq, comparator_32_eq, comparator_33_eq, comparator_34_eq, comparator_35_eq,
       comparator_36_eq, comparator_37_eq, comparator_38_eq, comparator_39_eq, comparator_40_eq,
       comparator_41_eq, comparator_42_eq, comparator_43_eq, comparator_44_eq, comparator_45_eq,
       comparator_46_eq, comparator_47_eq, comparator_48_eq, comparator_49_eq, comparator_50_eq,
       comparator_51_eq, comparator_52_eq, comparator_53_eq, comparator_54_eq, isAdd, isAddi, isAnd, isAndi,
       isAuipc, isBeq, isBge, isBgeu, isBlt, isBltu, isBne, isJal, isJalr, isLb, isLh, isLui, isLw, isMul,
       isMulh, isMulhu, isOr, isOri, isSb, isSh, isSll, isSlli, isSlt, isSlti, isSra, isSrai, isSri, isSrl,
       isSrli, isSub, isSw, isXor, isXori, IType, LType, not_1_out, not_2_out, not_3_out, or_1_out, RType,
       SType;
  wire [5:0] ROMinput;
  wire [15:14] rom_1_data;

  Comparator #(.width(7)) comparator_1 (.a(7'b0010011), .b(Instruction[6:0]), .eq(IType));  // open: gt, lt
  Comparator #(.width(7)) comparator_2 (.a(7'b0110011), .b(Instruction[6:0]), .eq(RType));  // open: gt, lt
  Comparator #(.width(7)) comparator_3 (.a(7'b1100011), .b(Instruction[6:0]), .eq(BType));  // open: gt, lt
  Comparator #(.width(7)) comparator_4 (.a(7'b0000011), .b(Instruction[6:0]), .eq(LType));  // open: gt, lt
  Comparator #(.width(7)) comparator_5 (.a(7'b0100011), .b(Instruction[6:0]), .eq(SType));  // open: gt, lt
  Comparator #(.width(7)) comparator_6 (.a(7'b0110111), .b(Instruction[6:0]), .eq(isLui));  // open: gt, lt
  Comparator #(.width(7)) comparator_7 (.a(7'b1101111), .b(Instruction[6:0]), .eq(isJal));  // open: gt, lt
  Comparator #(.width(7)) comparator_8 (.a(7'b1100111), .b(Instruction[6:0]), .eq(isJalr));  // open: gt, lt
  Comparator #(.width(7)) comparator_9 (.a(7'b0010111), .b(Instruction[6:0]), .eq(isAuipc));  // open: gt, lt
  ROM #(.addrWidth(6), .dataWidth(16)) rom_1 (
    .addr(ROMinput), .data({rom_1_data, WBSel, MemWEn, ALUSel, BSel, ASel, BrUn, ImmSel, RegWEn}));
  Comparator #(.width(3)) comparator_10 (.a(3'b000), .b(Instruction[14:12]), .eq(comparator_10_eq));  // open: gt, lt
  Comparator #(.width(3)) comparator_11 (.a(3'b111), .b(Instruction[14:12]), .eq(comparator_11_eq));  // open: gt, lt
  Comparator #(.width(3)) comparator_12 (.a(3'b110), .b(Instruction[14:12]), .eq(comparator_12_eq));  // open: gt, lt
  Comparator #(.width(3)) comparator_13 (.a(3'b100), .b(Instruction[14:12]), .eq(comparator_13_eq));  // open: gt, lt
  Comparator #(.width(3)) comparator_14 (.a(3'b001), .b(Instruction[14:12]), .eq(comparator_14_eq));  // open: gt, lt
  Comparator #(.width(3)) comparator_15 (.a(3'b101), .b(Instruction[14:12]), .eq(comparator_15_eq));  // open: gt, lt
  Comparator #(.width(7)) comparator_16 (.a({7{1'b0}}), .b(Instruction[31:25]), .eq(comparator_16_eq));  // open: gt, lt
  Comparator #(.width(7)) comparator_17 (
    .a(7'b0100000), .b(Instruction[31:25]), .eq(comparator_17_eq));  // open: gt, lt
  Comparator #(.width(3)) comparator_18 (.a(3'b010), .b(Instruction[14:12]), .eq(comparator_18_eq));  // open: gt, lt
  and and_1 (isAddi, IType, comparator_10_eq);
  and and_2 (isAndi, IType, comparator_11_eq);
  and and_3 (isOri, IType, comparator_12_eq);
  and and_4 (isXori, IType, comparator_13_eq);
  and and_5 (isSlli, IType, comparator_14_eq);
  and and_6 (isSri, IType, comparator_15_eq);
  and and_7 (isSrli, isSri, comparator_16_eq);
  and and_8 (isSrai, isSri, comparator_17_eq);
  and and_9 (isSlti, IType, comparator_18_eq);
  Comparator #(.width(7)) comparator_19 (.a({7{1'b0}}), .b(Instruction[31:25]), .eq(comparator_19_eq));  // open: gt, lt
  Comparator #(.width(3)) comparator_20 (.a(3'b000), .b(Instruction[14:12]), .eq(comparator_20_eq));  // open: gt, lt
  Comparator #(.width(7)) comparator_21 (
    .a(7'b0100000), .b(Instruction[31:25]), .eq(comparator_21_eq));  // open: gt, lt
  Comparator #(.width(3)) comparator_22 (.a(3'b000), .b(Instruction[14:12]), .eq(comparator_22_eq));  // open: gt, lt
  Comparator #(.width(7)) comparator_23 (.a({7{1'b0}}), .b(Instruction[31:25]), .eq(comparator_23_eq));  // open: gt, lt
  Comparator #(.width(3)) comparator_24 (.a(3'b111), .b(Instruction[14:12]), .eq(comparator_24_eq));  // open: gt, lt
  Comparator #(.width(7)) comparator_25 (.a({7{1'b0}}), .b(Instruction[31:25]), .eq(comparator_25_eq));  // open: gt, lt
  Comparator #(.width(3)) comparator_26 (.a(3'b110), .b(Instruction[14:12]), .eq(comparator_26_eq));  // open: gt, lt
  Comparator #(.width(7)) comparator_27 (.a({7{1'b0}}), .b(Instruction[31:25]), .eq(comparator_27_eq));  // open: gt, lt
  Comparator #(.width(3)) comparator_28 (.a(3'b100), .b(Instruction[14:12]), .eq(comparator_28_eq));  // open: gt, lt
  Comparator #(.width(7)) comparator_29 (.a({7{1'b0}}), .b(Instruction[31:25]), .eq(comparator_29_eq));  // open: gt, lt
  Comparator #(.width(3)) comparator_30 (.a(3'b001), .b(Instruction[14:12]), .eq(comparator_30_eq));  // open: gt, lt
  Comparator #(.width(7)) comparator_31 (.a({7{1'b0}}), .b(Instruction[31:25]), .eq(comparator_31_eq));  // open: gt, lt
  Comparator #(.width(3)) comparator_32 (.a(3'b101), .b(Instruction[14:12]), .eq(comparator_32_eq));  // open: gt, lt
  Comparator #(.width(7)) comparator_33 (
    .a(7'b0100000), .b(Instruction[31:25]), .eq(comparator_33_eq));  // open: gt, lt
  Comparator #(.width(3)) comparator_34 (.a(3'b101), .b(Instruction[14:12]), .eq(comparator_34_eq));  // open: gt, lt
  Comparator #(.width(7)) comparator_35 (.a({7{1'b0}}), .b(Instruction[31:25]), .eq(comparator_35_eq));  // open: gt, lt
  Comparator #(.width(3)) comparator_36 (.a(3'b010), .b(Instruction[14:12]), .eq(comparator_36_eq));  // open: gt, lt
  Comparator #(.width(7)) comparator_37 (
    .a(7'b0000001), .b(Instruction[31:25]), .eq(comparator_37_eq));  // open: gt, lt
  Comparator #(.width(3)) comparator_38 (.a(3'b000), .b(Instruction[14:12]), .eq(comparator_38_eq));  // open: gt, lt
  Comparator #(.width(7)) comparator_39 (
    .a(7'b0000001), .b(Instruction[31:25]), .eq(comparator_39_eq));  // open: gt, lt
  Comparator #(.width(3)) comparator_40 (.a(3'b001), .b(Instruction[14:12]), .eq(comparator_40_eq));  // open: gt, lt
  Comparator #(.width(7)) comparator_41 (
    .a(7'b0000001), .b(Instruction[31:25]), .eq(comparator_41_eq));  // open: gt, lt
  Comparator #(.width(3)) comparator_42 (.a(3'b011), .b(Instruction[14:12]), .eq(comparator_42_eq));  // open: gt, lt
  not not_1 (not_1_out, BrEq);
  and and_10 (isAdd, RType, comparator_19_eq, comparator_20_eq);
  and and_11 (isSub, RType, comparator_21_eq, comparator_22_eq);
  and and_12 (isAnd, RType, comparator_23_eq, comparator_24_eq);
  and and_13 (isOr, RType, comparator_25_eq, comparator_26_eq);
  and and_14 (isXor, RType, comparator_27_eq, comparator_28_eq);
  and and_15 (isSll, RType, comparator_29_eq, comparator_30_eq);
  and and_16 (isSrl, RType, comparator_31_eq, comparator_32_eq);
  and and_17 (isSra, RType, comparator_33_eq, comparator_34_eq);
  and and_18 (isSlt, RType, comparator_35_eq, comparator_36_eq);
  and and_19 (isMul, RType, comparator_37_eq, comparator_38_eq);
  and and_20 (isMulh, RType, comparator_39_eq, comparator_40_eq);
  and and_21 (isMulhu, RType, comparator_41_eq, comparator_42_eq);
  and and_22 (and_22_out, isBne, not_1_out);
  and and_23 (and_23_out, isBeq, BrEq);
  and and_24 (and_24_out, BrLt, isBlt);
  and and_25 (and_25_out, BrLt, isBltu);
  not not_2 (not_2_out, BrLt);
  and and_26 (and_26_out, not_2_out, isBge);
  not not_3 (not_3_out, BrLt);
  and and_27 (and_27_out, not_3_out, isBgeu);
  or or_1 (or_1_out, and_22_out, and_23_out, and_24_out, and_25_out, and_26_out, and_27_out);
  Comparator #(.width(3)) comparator_43 (.a(3'b000), .b(Instruction[14:12]), .eq(comparator_43_eq));  // open: gt, lt
  Comparator #(.width(3)) comparator_44 (.a(3'b101), .b(Instruction[14:12]), .eq(comparator_44_eq));  // open: gt, lt
  Comparator #(.width(3)) comparator_45 (.a(3'b111), .b(Instruction[14:12]), .eq(comparator_45_eq));  // open: gt, lt
  Comparator #(.width(3)) comparator_46 (.a(3'b100), .b(Instruction[14:12]), .eq(comparator_46_eq));  // open: gt, lt
  Comparator #(.width(3)) comparator_47 (.a(3'b110), .b(Instruction[14:12]), .eq(comparator_47_eq));  // open: gt, lt
  Comparator #(.width(3)) comparator_48 (.a(3'b001), .b(Instruction[14:12]), .eq(comparator_48_eq));  // open: gt, lt
  or or_2 (PCSel, isJal, isJalr, or_1_out);
  and and_28 (isBeq, BType, comparator_43_eq);
  and and_29 (isBge, BType, comparator_44_eq);
  and and_30 (isBgeu, BType, comparator_45_eq);
  and and_31 (isBlt, BType, comparator_46_eq);
  and and_32 (isBltu, BType, comparator_47_eq);
  and and_33 (isBne, BType, comparator_48_eq);
  Comparator #(.width(3)) comparator_49 (.a(3'b000), .b(Instruction[14:12]), .eq(comparator_49_eq));  // open: gt, lt
  Comparator #(.width(3)) comparator_50 (.a(3'b001), .b(Instruction[14:12]), .eq(comparator_50_eq));  // open: gt, lt
  Comparator #(.width(3)) comparator_51 (.a(3'b010), .b(Instruction[14:12]), .eq(comparator_51_eq));  // open: gt, lt
  Comparator #(.width(3)) comparator_52 (.a(3'b000), .b(Instruction[14:12]), .eq(comparator_52_eq));  // open: gt, lt
  Comparator #(.width(3)) comparator_53 (.a(3'b001), .b(Instruction[14:12]), .eq(comparator_53_eq));  // open: gt, lt
  Comparator #(.width(3)) comparator_54 (.a(3'b010), .b(Instruction[14:12]), .eq(comparator_54_eq));  // open: gt, lt
  and and_34 (isLb, LType, comparator_49_eq);
  and and_35 (isLh, LType, comparator_50_eq);
  and and_36 (isLw, LType, comparator_51_eq);
  and and_37 (isSb, SType, comparator_52_eq);
  and and_38 (isSh, SType, comparator_53_eq);
  and and_39 (isSw, SType, comparator_54_eq);
  Priority_Encoder #(.select_enc(6)) priority_encoder_1 (
    .in0(isAdd), .in1(isMul), .in2(isSub), .in3(isSll), .in4(isMulh), .in5(isMulhu), .in6(isSlt),
    .in7(isXor), .in8(isSrl), .in9(isSra), .in10(isOr), .in11(isAnd), .in12(isLb), .in13(isLh), .in14(isLw),
    .in15(isAddi), .in16(isSlli), .in17(isSlti), .in18(isXori), .in19(isSrli), .in20(isSrai), .in21(isOri),
    .in22(isAndi), .in23(isSb), .in24(isSh), .in25(isSw), .in26(isBeq), .in27(isBne), .in28(isBlt),
    .in29(isBge), .in30(isBltu), .in31(isBgeu), .in32(isAuipc), .in33(isLui), .in34(isJal), .in35(isJalr),
    .out(ROMinput));  // open: in36, in37, in38, in39, in40, in41, in42, in43, in44, in45, in46, in47, in48, in49, in50, in51, in52, in53, in54, in55, in56, in57, in58, in59, in60, in61, in62, in63, gs, en_out, en_in

  // Other names for the same wires on the sheet: opcode[6:0] = Instruction[6:0]; rd[4:0] = Instruction[11:7];
  //   funct3[2:0] = Instruction[14:12]; rs1[4:0] = Instruction[19:15]; rs2[4:0] = Instruction[24:20];
  //   funct7[6:0] = Instruction[31:25]

  // Notes on the sheet:
  //   INPUTS to your circuit
  //   contents of rom_1 (hex, n*v repeats v):
  //   1001 1401 1601 1081 1481 1581 1101 1201 1281 1681 1301 1381 2041 2041 2041 1041 10c1 1141 1241 12c1
  //   16c1 1341 13c1 842 842 842 4*64 74 74 1067 17c7 69 41
  //   ROM FOR CONTROL LOGIC
  //   DON'T CHANGE THE LOCATIONS OF THE INPUTS AND OUTPUTS!
  //   This is only if you choose to do the ROM option
  //   CONNECT
  //   WIRE
  //   USE
  //   ROM
  //   OUTPUT from your circuit
  //   Reminder: If using ROM, use combinational logic for PCSel
endmodule
